// Logisim project semaforos.circ as structural Verilog: 4 circuits, main circuit main
module main (
  input  bpsv
);

  wire display_1_a, display_1_b, display_1_c, display_1_d, display_1_e, display_1_f, display_1_g,
       semaforo_carros_ac, semaforo_carros_vc, semaforo_carros_vrc, semaforo_peoes_ap, semaforo_peoes_vp,
       semaforo_peoes_vrp, semaforo_peoes_x0, semaforo_peoes_x1, semaforo_peoes_x2, semaforo_peoes_x3;

  semaforo_carros semaforo_carros (
    .bpsv(bpsv), .vrp(semaforo_peoes_vrp), .vrc(semaforo_carros_vrc), .ac(semaforo_carros_ac),
    .vc(semaforo_carros_vc));
  semaforo_peoes semaforo_peoes (
    .vrc(semaforo_carros_vrc), .vrp(semaforo_peoes_vrp), .ap(semaforo_peoes_ap), .vp(semaforo_peoes_vp),
    .x0(semaforo_peoes_x0), .x1(semaforo_peoes_x1), .x2(semaforo_peoes_x2), .x3(semaforo_peoes_x3));
  LED led_1 (.in(semaforo_carros_vrc));
  LED led_2 (.in(semaforo_carros_ac));
  LED led_3 (.in(semaforo_carros_vc));
  LED led_4 (.in(semaforo_peoes_vrp));
  LED led_5 (.in(semaforo_peoes_ap));
  LED led_6 (.in(semaforo_peoes_vp));
  Display display_1 (
    .x0(semaforo_peoes_x0), .x1(semaforo_peoes_x1), .x2(semaforo_peoes_x2), .x3(semaforo_peoes_x3),
    .a(display_1_a), .b(display_1_b), .c(display_1_c), .d(display_1_d), .e(display_1_e), .f(display_1_f),
    .g(display_1_g));
  _7_Segment_Display u_7_segment_display_1 (
    .g(display_1_a), .f(display_1_b), .a(display_1_c), .b(display_1_d), .e(display_1_e), .d(display_1_f),
    .c(display_1_g));  // open: dp
endmodule

module semaforo_carros (
  input  bpsv,
  input  vrp,
  output vrc,
  output ac,
  output vc
);

  wire and_1_out, and_2_out, and_3_out, and_5_out, and_6_out, and_7_out, and_8_out, and_9_out, and_10_out,
       clock_1_out, d0_q, d1_q, d2_q, not_1_out, not_2_out, not_3_out, not_4_out, not_5_out, not_6_out,
       not_7_out, not_8_out, not_9_out, not_10_out, not_11_out, not_12_out, not_13_out, not_14_out, or_3_out,
       or_4_out;

  Clock clock_1 (.out(clock_1_out));
  or or_1 (vrc, d0_q, d1_q);
  not not_1 (not_1_out, d0_q);
  not not_2 (not_2_out, d1_q);
  not not_3 (not_3_out, d1_q);
  not not_4 (not_4_out, bpsv);
  not not_5 (not_5_out, d0_q);
  not not_6 (not_6_out, d1_q);
  not not_7 (not_7_out, d2_q);
  and and_1 (and_1_out, vrp, d1_q, d2_q);
  not not_8 (not_8_out, d1_q);
  not not_9 (not_9_out, d2_q);
  not not_10 (not_10_out, vrp);
  not not_11 (not_11_out, vrp);
  not not_12 (not_12_out, d2_q);
  not not_13 (not_13_out, d0_q);
  not not_14 (not_14_out, d2_q);
  and and_2 (and_2_out, not_1_out, not_2_out, bpsv);
  and and_3 (and_3_out, not_3_out, d2_q);
  and and_4 (vc, not_4_out, not_5_out, not_6_out, not_7_out);
  and and_5 (and_5_out, not_8_out, d2_q);
  and and_6 (and_6_out, d1_q, not_9_out);
  and and_7 (and_7_out, not_10_out, d1_q);
  and and_8 (and_8_out, not_11_out, d1_q);
  and and_9 (and_9_out, d1_q, not_12_out);
  and and_10 (and_10_out, bpsv, not_13_out, not_14_out);
  or or_2 (ac, and_2_out, and_3_out);
  or or_3 (or_3_out, and_5_out, and_6_out, and_7_out);
  or or_4 (or_4_out, and_8_out, and_9_out, and_10_out);
  D_Flip_Flop d0 (.clk(clock_1_out), .D(and_1_out), .Q(d0_q));  // open: Qn, preset, en, reset
  D_Flip_Flop d1 (.clk(clock_1_out), .D(or_3_out), .Q(d1_q));  // open: Qn, preset, en, reset
  D_Flip_Flop d2 (.clk(clock_1_out), .D(or_4_out), .Q(d2_q));  // open: Qn, preset, en, reset
endmodule

module semaforo_peoes (
  input  vrc,
  output vrp,
  output ap,
  output vp,
  output x0,
  output x1,
  output x2,
  output x3
);

  wire and_3_out, and_4_out, and_5_out, and_6_out, and_7_out, and_8_out, and_9_out, and_10_out, and_11_out,
       and_12_out, and_13_out, and_14_out, and_15_out, and_16_out, clock_1_out, not_1_out, not_2_out,
       not_3_out, not_4_out, not_5_out, not_6_out, not_7_out, not_8_out, not_9_out, not_10_out, not_11_out,
       not_12_out, not_13_out, not_14_out, not_15_out, not_16_out, not_17_out, not_18_out, or_2_out,
       or_3_out, or_4_out, or_5_out;

  Clock clock_1 (.out(clock_1_out));
  not not_1 (not_1_out, x0);
  not not_2 (not_2_out, x1);
  not not_3 (not_3_out, x2);
  and and_1 (ap, x0, x2);
  not not_4 (not_4_out, x0);
  not not_5 (not_5_out, x2);
  not not_6 (not_6_out, x2);
  not not_7 (not_7_out, x3);
  not not_8 (not_8_out, x0);
  not not_9 (not_9_out, x1);
  not not_10 (not_10_out, x2);
  not not_11 (not_11_out, x3);
  not not_12 (not_12_out, x2);
  not not_13 (not_13_out, x3);
  not not_14 (not_14_out, vrc);
  not not_15 (not_15_out, x3);
  not not_16 (not_16_out, x3);
  not not_17 (not_17_out, x3);
  not not_18 (not_18_out, x3);
  and and_2 (vrp, not_1_out, not_2_out, not_3_out);
  and and_3 (and_3_out, not_4_out, x2);
  and and_4 (and_4_out, x0, not_5_out);
  and and_5 (and_5_out, x1, x2, x3);
  and and_6 (and_6_out, x0, not_6_out);
  and and_7 (and_7_out, x0, not_7_out);
  and and_8 (and_8_out, not_8_out, not_9_out, x2, x3);
  and and_9 (and_9_out, x1, not_10_out);
  and and_10 (and_10_out, x1, not_11_out);
  and and_11 (and_11_out, not_12_out, x3);
  and and_12 (and_12_out, x2, not_13_out);
  and and_13 (and_13_out, not_14_out, not_15_out);
  and and_14 (and_14_out, x2, not_16_out);
  and and_15 (and_15_out, x1, not_17_out);
  and and_16 (and_16_out, x0, not_18_out);
  or or_1 (vp, and_3_out, x1, and_4_out);
  or or_2 (or_2_out, and_5_out, and_6_out, and_7_out);
  or or_3 (or_3_out, and_8_out, and_9_out, and_10_out);
  or or_4 (or_4_out, and_11_out, and_12_out);
  or or_5 (or_5_out, and_13_out, and_14_out, and_15_out, and_16_out);
  D_Flip_Flop d0 (.clk(clock_1_out), .D(or_2_out), .Q(x0));  // open: Qn, preset, en, reset
  D_Flip_Flop d1 (.clk(clock_1_out), .D(or_3_out), .Q(x1));  // open: Qn, preset, en, reset
  D_Flip_Flop d2 (.clk(clock_1_out), .D(or_4_out), .Q(x2));  // open: Qn, preset, en, reset
  D_Flip_Flop d3 (.clk(clock_1_out), .D(or_5_out), .Q(x3));  // open: Qn, preset, en, reset
endmodule

module Display (
  input  x0,
  input  x1,
  input  x2,
  input  x3,
  output a,
  output b,
  output c,
  output d,
  output e,
  output f,
  output g
);

  wire and_1_out, and_2_out, and_3_out, and_4_out, and_5_out, and_6_out, and_7_out, and_8_out, and_9_out,
       and_10_out, and_11_out, and_12_out, and_13_out, and_14_out, and_15_out, and_16_out, and_17_out,
       and_18_out, and_19_out, and_20_out, and_21_out, not_1_out, not_2_out, not_3_out, not_4_out, not_5_out,
       not_6_out, not_7_out, not_8_out, not_9_out, not_10_out, not_11_out, not_12_out, not_13_out,
       not_14_out, not_15_out, not_16_out, not_17_out, not_18_out, not_19_out, not_20_out, not_21_out,
       not_22_out, not_23_out, not_24_out, not_25_out, not_26_out, not_27_out, not_28_out, not_29_out,
       not_30_out, not_31_out, not_32_out, not_33_out, not_34_out, not_35_out, not_36_out, not_37_out,
       not_38_out, not_39_out, not_40_out, not_41_out, not_42_out, not_43_out;

  not not_1 (not_1_out, x0);
  not not_2 (not_2_out, x3);
  not not_3 (not_3_out, x0);
  not not_4 (not_4_out, x1);
  not not_5 (not_5_out, x2);
  not not_6 (not_6_out, x3);
  not not_7 (not_7_out, x0);
  and and_1 (and_1_out, not_7_out, x2, not_8_out);
  not not_8 (not_8_out, x3);
  not not_9 (not_9_out, x0);
  and and_2 (and_2_out, not_9_out, x1, not_10_out);
  not not_10 (not_10_out, x2);
  not not_11 (not_11_out, x0);
  not not_12 (not_12_out, x1);
  not not_13 (not_13_out, x0);
  not not_14 (not_14_out, x2);
  not not_15 (not_15_out, x0);
  not not_16 (not_16_out, x1);
  not not_17 (not_17_out, x2);
  not not_18 (not_18_out, x3);
  not not_19 (not_19_out, x0);
  and and_3 (and_3_out, not_19_out, x2);
  not not_20 (not_20_out, x1);
  and and_4 (and_4_out, x0, not_20_out, not_21_out);
  not not_21 (not_21_out, x2);
  not not_22 (not_22_out, x0);
  not not_23 (not_23_out, x1);
  not not_24 (not_24_out, x3);
  not not_25 (not_25_out, x0);
  not not_26 (not_26_out, x2);
  not not_27 (not_27_out, x3);
  not not_28 (not_28_out, x1);
  not not_29 (not_29_out, x2);
  not not_30 (not_30_out, x3);
  not not_31 (not_31_out, x0);
  not not_32 (not_32_out, x1);
  not not_33 (not_33_out, x3);
  not not_34 (not_34_out, x0);
  not not_35 (not_35_out, x2);
  not not_36 (not_36_out, x0);
  not not_37 (not_37_out, x1);
  not not_38 (not_38_out, x2);
  not not_39 (not_39_out, x3);
  not not_40 (not_40_out, x0);
  not not_41 (not_41_out, x0);
  not not_42 (not_42_out, x1);
  not not_43 (not_43_out, x2);
  and and_5 (and_5_out, not_1_out, x2, not_2_out);
  or or_1 (a, and_5_out, and_6_out, and_7_out);
  and and_6 (and_6_out, not_3_out, x1);
  and and_7 (and_7_out, x0, not_4_out, not_5_out, not_6_out);
  or or_2 (b, and_1_out, and_2_out);
  and and_8 (and_8_out, not_11_out, not_12_out, x2);
  and and_9 (and_9_out, not_13_out, x1, not_14_out);
  and and_10 (and_10_out, not_15_out, x1, x3);
  and and_11 (and_11_out, x0, not_16_out, not_17_out, not_18_out);
  or or_3 (d, and_3_out, and_4_out);
  and and_12 (and_12_out, not_22_out, not_23_out, x2, not_24_out);
  or or_4 (e, and_12_out, and_13_out, and_14_out);
  and and_13 (and_13_out, not_25_out, x1, not_26_out, not_27_out);
  and and_14 (and_14_out, x0, not_28_out, not_29_out, not_30_out);
  and and_15 (and_15_out, not_31_out, not_32_out, x2, not_33_out);
  and and_16 (and_16_out, not_34_out, x1, not_35_out);
  and and_17 (and_17_out, not_36_out, x1, x3);
  and and_18 (and_18_out, x0, not_37_out, not_38_out, not_39_out);
  and and_19 (and_19_out, not_40_out, x2);
  and and_20 (and_20_out, not_41_out, x1);
  or or_5 (g, and_19_out, and_20_out, and_21_out);
  and and_21 (and_21_out, x0, not_42_out, not_43_out, x3);
  or or_6 (c, and_8_out, and_9_out, and_10_out, and_11_out);
  or or_7 (f, and_15_out, and_16_out, and_17_out, and_18_out);
endmodule
